# Fritzing sketch led_memorization_ir_breadboard (saved by Fritzing 0.9.3b)
breadboards: 1

parts:
  Part1 = Arduino Uno (Rev3)
  LED1 = LED - 5mm [color="Yellow (585nm)" package="5 mm [THT]"]
  LED3 = LED - 5mm [color="Blue (505nm)" package="5 mm [THT]"]
  LED2 = LED - 5mm [color="Red (633nm)" package="5 mm [THT]"]
  *IR_receiver_pinout_may_vary = TSOP312.., 314.. [package=THT]
  R1 = Resistor [tolerance=±5% resistance=220 package="1206 [SMD]"]
  R2 = Resistor [tolerance=±5% resistance=220 package="1206 [SMD]"]
  R3 = Resistor [tolerance=±5% resistance=220 package="1206 [SMD]"]

nets:
  N1: Part1.D2, *IR_receiver_pinout_may_vary.Data
  N2: Part1.D5_PWM, LED3.anode
  N3: Part1.D6_PWM, LED2.anode
  N4: Part1.D7, LED1.anode
  N5: Part1.5V, *IR_receiver_pinout_may_vary.Vs
  GND: Part1.GND, *IR_receiver_pinout_may_vary.GND, R1.Pin_0, R2.Pin_0, R3.Pin_0
  N6: LED1.cathode, R1.Pin_1
  N7: LED3.cathode, R3.Pin_1
  N8: LED2.cathode, R2.Pin_1
