# Fritzing sketch led_memorization_analog_breadboard (saved by Fritzing 0.9.3b)
breadboards: 1

parts:
  Part1 = Arduino Uno (Rev3)
  S1 = Pushbutton [package="[THT]"]
  S3 = Pushbutton [package="[THT]"]
  S4 = Pushbutton [package="[THT]"]
  R1 = Resistor [tolerance=±5% resistance=220 package=THT]
  R2 = Resistor [tolerance=±5% resistance=10k package=THT]
  R3 = Resistor [tolerance=±5% resistance=10k package=THT]
  LED1 = LED - 5mm [color="Yellow (585nm)" package="5 mm [THT]"]
  LED3 = LED - 5mm [color="Blue (505nm)" package="5 mm [THT]"]
  R4 = Resistor [tolerance=±5% resistance=220 package=THT]
  R5 = Resistor [tolerance=±5% resistance=220 package=THT]
  R6 = Resistor [tolerance=±5% resistance=220 package=THT]
  S2 = Pushbutton [package="[THT]"]
  LED2 = LED - 5mm [color="Red (633nm)" package="5 mm [THT]"]
  R7 = Resistor [tolerance=±5% resistance=10k package=THT]

nets:
  N1: Part1.A0, S3.Pin_1, S3.Pin_2, S4.Pin_1, S4.Pin_2, R3.Pin_1, S2.Pin_1, S2.Pin_2
  N2: Part1.D2, S1.Pin_3, S1.Pin_4, R7.Pin_1
  N3: Part1.D5_PWM, LED3.anode
  N4: Part1.D6_PWM, LED2.anode
  N5: Part1.D7, LED1.anode
  N6: Part1.5V, S1.Pin_1, S1.Pin_2, S4.Pin_3, S4.Pin_4, R1.Pin_0, R2.Pin_0
  N7: Part1.GND, R3.Pin_0, R4.Pin_0, R5.Pin_0, R6.Pin_0, R7.Pin_0
  N8: S3.Pin_3, S3.Pin_4, R1.Pin_1
  N9: R2.Pin_1, S2.Pin_3, S2.Pin_4
  N10: LED1.cathode, R6.Pin_1
  N11: LED3.cathode, R4.Pin_1
  N12: R5.Pin_1, LED2.cathode
